// Logisim project mips_lite.circ as structural Verilog: 12 circuits, main circuit main
module main (
  input  in_1
);

  wire ALUSrc, clk, j, MemtoReg, MemWr, pc_sel, RegDst, RegWr, zero;
  wire [1:0] ALUctr, ExtOp;
  wire [4:0] IFU_6_10, IFU_11_15, IFU_16_20, IFU_21_25, multiplexer_1_out;
  wire [5:0] IFU_0_5, IFU_26_31;
  wire [31:0] busW, multiplexer_2_out, n18020208_alu_1_result, n18020208_dm_1_out_6, n18020208_ext_1_b,
       n18020208_gpr_1_busa, n18020208_gpr_1_busb;

  _18020208_IFU u_18020208_ifu_1 (
    .insout({IFU_26_31, IFU_21_25, IFU_16_20, IFU_11_15, IFU_6_10, IFU_0_5}), .npc_sel(pc_sel), .zero(zero),
    .clk(clk), .reset(in_1), .j(j));
  _18020208_CONTROL u_18020208_control_1 (
    .opcode(IFU_26_31), .\function (IFU_0_5), .RegDst(RegDst), .ALUSrc(ALUSrc), .MemtoReg(MemtoReg),
    .RegWrite(RegWr), .MemWrite(MemWr), .npc_sel(pc_sel), .ExtOp(ExtOp), .ALUCtr(ALUctr), .j(j));
  Multiplexer #(.select(1), .width(5), .disabled("Z"), .enable("false")) multiplexer_1 (
    .in0(IFU_16_20), .in1(IFU_11_15), .out(multiplexer_1_out), .sel(RegDst));
  _18020208_GPR u_18020208_gpr_1 (
    .clk(clk), .RegWr(RegWr), .rw(multiplexer_1_out), .busw(busW), .busa(n18020208_gpr_1_busa),
    .busb(n18020208_gpr_1_busb), .reset(in_1), .ra(IFU_21_25), .rb(IFU_16_20));
  _18020208_EXT u_18020208_ext_1 (.A({IFU_11_15, IFU_6_10, IFU_0_5}), .B(n18020208_ext_1_b), .ExtOp(ExtOp));
  Clock #(.highDuration(1), .lowDuration(1)) clock_1 (.out(clk));
  Multiplexer #(.select(1), .width(32), .disabled("Z"), .enable("false")) multiplexer_2 (
    .in0(n18020208_gpr_1_busb), .in1(n18020208_ext_1_b), .out(multiplexer_2_out), .sel(ALUSrc));
  // Probe on n18020208_alu_1_result
  _18020208_ALU u_18020208_alu_1 (
    .A(n18020208_gpr_1_busa), .B(multiplexer_2_out), .result(n18020208_alu_1_result), .ALUctr(ALUctr));
  _18020208_DM u_18020208_dm_1 (
    .in_1(in_1), .in_2(clk), .in_3(MemWr), .addr(n18020208_alu_1_result), .data_in(n18020208_gpr_1_busb),
    .out_6(n18020208_dm_1_out_6));
  nor nor_1 (zero, n18020208_alu_1_result[0], n18020208_alu_1_result[1], n18020208_alu_1_result[2], n18020208_alu_1_result[3], n18020208_alu_1_result[4], n18020208_alu_1_result[5], n18020208_alu_1_result[6], n18020208_alu_1_result[7], n18020208_alu_1_result[8], n18020208_alu_1_result[9], n18020208_alu_1_result[10], n18020208_alu_1_result[11], n18020208_alu_1_result[12], n18020208_alu_1_result[13], n18020208_alu_1_result[14], n18020208_alu_1_result[15], n18020208_alu_1_result[17], n18020208_alu_1_result[18], n18020208_alu_1_result[19], n18020208_alu_1_result[20], n18020208_alu_1_result[21], n18020208_alu_1_result[22], n18020208_alu_1_result[23], n18020208_alu_1_result[24], n18020208_alu_1_result[25], n18020208_alu_1_result[26], n18020208_alu_1_result[27], n18020208_alu_1_result[28], n18020208_alu_1_result[29], n18020208_alu_1_result[30], n18020208_alu_1_result[31], n18020208_alu_1_result[16]);
  Multiplexer #(.select(1), .width(32), .disabled("Z"), .enable("false")) multiplexer_3 (
    .in0(n18020208_alu_1_result), .in1(n18020208_dm_1_out_6), .out(busW), .sel(MemtoReg));

  // Other names for the same wires on the sheet: reset = in_1
endmodule

// GPR
module _18020208_GPR (
  input  reset,
  input  clk,
  input  RegWr,
  input  [4:0] rw,
  input  [4:0] ra,
  input  [4:0] rb,
  input  [31:0] busw,
  output [31:0] busa,
  output [31:0] busb
);

  wire demultiplexer_1_out1, demultiplexer_1_out2, demultiplexer_1_out3, demultiplexer_1_out4,
       demultiplexer_1_out5, demultiplexer_1_out6, demultiplexer_1_out7, demultiplexer_1_out8,
       demultiplexer_1_out9, demultiplexer_1_out10, demultiplexer_1_out11, demultiplexer_1_out12,
       demultiplexer_1_out13, demultiplexer_1_out14, demultiplexer_1_out15, demultiplexer_1_out16,
       demultiplexer_1_out17, demultiplexer_1_out18, demultiplexer_1_out19, demultiplexer_1_out20,
       demultiplexer_1_out21, demultiplexer_1_out22, demultiplexer_1_out23, demultiplexer_1_out24,
       demultiplexer_1_out25, demultiplexer_1_out26, demultiplexer_1_out27, demultiplexer_1_out28,
       demultiplexer_1_out29, demultiplexer_1_out30, demultiplexer_1_out31;
  wire [31:0] _0, _1, _2, _3, _4, _5, _6, _7, _8, _9, _10, _11, _12, _13, _14, _15, _16, _17, _18, _19, _20,
       _21, _22, _23, _24, _25, _26, _27, _28, _29, _30, _31;

  Demultiplexer #(.select(5), .width(1), .tristate("false"), .disabled("Z"), .enable("false")) demultiplexer_1 (
    .out1(demultiplexer_1_out1), .out2(demultiplexer_1_out2), .out3(demultiplexer_1_out3),
    .out4(demultiplexer_1_out4), .out5(demultiplexer_1_out5), .out6(demultiplexer_1_out6),
    .out7(demultiplexer_1_out7), .out8(demultiplexer_1_out8), .out9(demultiplexer_1_out9),
    .out10(demultiplexer_1_out10), .out11(demultiplexer_1_out11), .out12(demultiplexer_1_out12),
    .out13(demultiplexer_1_out13), .out14(demultiplexer_1_out14), .out15(demultiplexer_1_out15),
    .out16(demultiplexer_1_out16), .out17(demultiplexer_1_out17), .out18(demultiplexer_1_out18),
    .out19(demultiplexer_1_out19), .out20(demultiplexer_1_out20), .out21(demultiplexer_1_out21),
    .out22(demultiplexer_1_out22), .out23(demultiplexer_1_out23), .out24(demultiplexer_1_out24),
    .out25(demultiplexer_1_out25), .out26(demultiplexer_1_out26), .out27(demultiplexer_1_out27),
    .out28(demultiplexer_1_out28), .out29(demultiplexer_1_out29), .out30(demultiplexer_1_out30),
    .out31(demultiplexer_1_out31), .in(RegWr), .sel(rw));  // open: out0
  Register #(.width(32), .trigger("rising"), .Select("low")) u__0 (.Q(_0), .clk(clk), .clr(reset));  // open: D, en
  Register #(.width(32), .trigger("rising"), .Select("low")) u__1 (
    .D(busw), .en(demultiplexer_1_out1), .Q(_1), .clk(clk), .clr(reset));
  Register #(.width(32), .trigger("rising"), .Select("low")) u__2 (
    .D(busw), .en(demultiplexer_1_out2), .Q(_2), .clk(clk), .clr(reset));
  Register #(.width(32), .trigger("rising"), .Select("low")) u__3 (
    .D(busw), .en(demultiplexer_1_out3), .Q(_3), .clk(clk), .clr(reset));
  Register #(.width(32), .trigger("rising"), .Select("low")) u__4 (
    .D(busw), .en(demultiplexer_1_out4), .Q(_4), .clk(clk), .clr(reset));
  Register #(.width(32), .trigger("rising"), .Select("low")) u__5 (
    .D(busw), .en(demultiplexer_1_out5), .Q(_5), .clk(clk), .clr(reset));
  Register #(.width(32), .trigger("rising"), .Select("low")) u__6 (
    .D(busw), .en(demultiplexer_1_out6), .Q(_6), .clk(clk), .clr(reset));
  Register #(.width(32), .trigger("rising"), .Select("low")) u__7 (
    .D(busw), .en(demultiplexer_1_out7), .Q(_7), .clk(clk), .clr(reset));
  Register #(.width(32), .trigger("rising"), .Select("low")) u__8 (
    .D(busw), .en(demultiplexer_1_out8), .Q(_8), .clk(clk), .clr(reset));
  Register #(.width(32), .trigger("rising"), .Select("low")) u__9 (
    .D(busw), .en(demultiplexer_1_out9), .Q(_9), .clk(clk), .clr(reset));
  Register #(.width(32), .trigger("rising"), .Select("low")) u__10 (
    .D(busw), .en(demultiplexer_1_out10), .Q(_10), .clk(clk), .clr(reset));
  Register #(.width(32), .trigger("rising"), .Select("low")) u__11 (
    .D(busw), .en(demultiplexer_1_out11), .Q(_11), .clk(clk), .clr(reset));
  Register #(.width(32), .trigger("rising"), .Select("low")) u__12 (
    .D(busw), .en(demultiplexer_1_out12), .Q(_12), .clk(clk), .clr(reset));
  Register #(.width(32), .trigger("rising"), .Select("low")) u__13 (
    .D(busw), .en(demultiplexer_1_out13), .Q(_13), .clk(clk), .clr(reset));
  Register #(.width(32), .trigger("rising"), .Select("low")) u__14 (
    .D(busw), .en(demultiplexer_1_out14), .Q(_14), .clk(clk), .clr(reset));
  Register #(.width(32), .trigger("rising"), .Select("low")) u__15 (
    .D(busw), .en(demultiplexer_1_out15), .Q(_15), .clk(clk), .clr(reset));
  Register #(.width(32), .trigger("rising"), .Select("low")) u__16 (
    .D(busw), .en(demultiplexer_1_out16), .Q(_16), .clk(clk), .clr(reset));
  Register #(.width(32), .trigger("rising"), .Select("low")) u__17 (
    .D(busw), .en(demultiplexer_1_out17), .Q(_17), .clk(clk), .clr(reset));
  Register #(.width(32), .trigger("rising"), .Select("low")) u__18 (
    .D(busw), .en(demultiplexer_1_out18), .Q(_18), .clk(clk), .clr(reset));
  Register #(.width(32), .trigger("rising"), .Select("low")) u__19 (
    .D(busw), .en(demultiplexer_1_out19), .Q(_19), .clk(clk), .clr(reset));
  Register #(.width(32), .trigger("rising"), .Select("low")) u__20 (
    .D(busw), .en(demultiplexer_1_out20), .Q(_20), .clk(clk), .clr(reset));
  Register #(.width(32), .trigger("rising"), .Select("low")) u__21 (
    .D(busw), .en(demultiplexer_1_out21), .Q(_21), .clk(clk), .clr(reset));
  Register #(.width(32), .trigger("rising"), .Select("low")) u__22 (
    .D(busw), .en(demultiplexer_1_out22), .Q(_22), .clk(clk), .clr(reset));
  Register #(.width(32), .trigger("rising"), .Select("low")) u__23 (
    .D(busw), .en(demultiplexer_1_out23), .Q(_23), .clk(clk), .clr(reset));
  Register #(.width(32), .trigger("rising"), .Select("low")) u__24 (
    .D(busw), .en(demultiplexer_1_out24), .Q(_24), .clk(clk), .clr(reset));
  Register #(.width(32), .trigger("rising"), .Select("low")) u__25 (
    .D(busw), .en(demultiplexer_1_out25), .Q(_25), .clk(clk), .clr(reset));
  Register #(.width(32), .trigger("rising"), .Select("low")) u__26 (
    .D(busw), .en(demultiplexer_1_out26), .Q(_26), .clk(clk), .clr(reset));
  Register #(.width(32), .trigger("rising"), .Select("low")) u__27 (
    .D(busw), .en(demultiplexer_1_out27), .Q(_27), .clk(clk), .clr(reset));
  Register #(.width(32), .trigger("rising"), .Select("low")) u__28 (
    .D(busw), .en(demultiplexer_1_out28), .Q(_28), .clk(clk), .clr(reset));
  Register #(.width(32), .trigger("rising"), .Select("low")) u__29 (
    .D(busw), .en(demultiplexer_1_out29), .Q(_29), .clk(clk), .clr(reset));
  Register #(.width(32), .trigger("rising"), .Select("low")) u__30 (
    .D(busw), .en(demultiplexer_1_out30), .Q(_30), .clk(clk), .clr(reset));
  Register #(.width(32), .trigger("rising"), .Select("low")) u__31 (
    .D(busw), .en(demultiplexer_1_out31), .Q(_31), .clk(clk), .clr(reset));
  Multiplexer #(.select(5), .width(32), .disabled("Z"), .enable("false")) multiplexer_1 (
    .in0(_0), .in1(_1), .in2(_2), .in3(_3), .in4(_4), .in5(_5), .in6(_6), .in7(_7), .in8(_8), .in9(_9),
    .in10(_10), .in11(_11), .in12(_12), .in13(_13), .in14(_14), .in15(_15), .in16(_16), .in17(_17),
    .in18(_18), .in19(_19), .in20(_20), .in21(_21), .in22(_22), .in23(_23), .in24(_24), .in25(_25),
    .in26(_26), .in27(_27), .in28(_28), .in29(_29), .in30(_30), .in31(_31), .out(busa), .sel(ra));
  Multiplexer #(.select(5), .width(32), .disabled("Z"), .enable("false")) multiplexer_2 (
    .in0(_0), .in1(_1), .in2(_2), .in3(_3), .in4(_4), .in5(_5), .in6(_6), .in7(_7), .in8(_8), .in9(_9),
    .in10(_10), .in11(_11), .in12(_12), .in13(_13), .in14(_14), .in15(_15), .in16(_16), .in17(_17),
    .in18(_18), .in19(_19), .in20(_20), .in21(_21), .in22(_22), .in23(_23), .in24(_24), .in25(_25),
    .in26(_26), .in27(_27), .in28(_28), .in29(_29), .in30(_30), .in31(_31), .out(busb), .sel(rb));
endmodule

// IFU
module _18020208_IFU (
  input  j,
  input  clk,
  input  reset,
  input  npc_sel,
  input  zero,
  output [31:0] insout
);

  wire and_1_out;
  wire [3:0] pc_31_28;
  wire [27:0] pc_q;
  wire [31:0] adder_1_out, adder_2_out, bit_extender_1_out, multiplexer_1_out, multiplexer_2_out,
       shifter_1_out;

  assign bit_extender_1_out = {{16{insout[15]}}, insout[15:0]};  // Bit_Extender bit_extender_1
  Shifter #(.width(32), .shift("ll")) shifter_1 (.in(bit_extender_1_out), .\dist (5'b00010), .out(shifter_1_out));
  Adder #(.width(32)) adder_1 (.a({pc_31_28, pc_q}), .b(32'h4), .out(adder_1_out));  // open: cin, cout
  Adder #(.width(32)) adder_2 (.a(adder_1_out), .b(shifter_1_out), .out(adder_2_out));  // open: cin, cout
  and and_1 (and_1_out, npc_sel, zero);
  Multiplexer #(.select(1), .width(32), .disabled("Z"), .enable("false")) multiplexer_1 (
    .in0(adder_1_out), .in1(adder_2_out), .out(multiplexer_1_out), .sel(and_1_out));
  Register #(.width(32), .trigger("rising"), .Select("low")) pc (
    .D(multiplexer_2_out), .Q({pc_31_28, pc_q}), .clk(clk), .clr(reset));  // open: en
  Multiplexer #(.select(1), .width(32), .disabled("Z"), .enable("false")) multiplexer_2 (
    .in0(multiplexer_1_out), .in1({pc_31_28, insout[25:0], 2'b00}), .out(multiplexer_2_out), .sel(j));
  ROM #(.addrWidth(8), .dataWidth(8), .Select("low")) RAM3 (.addr(pc_q[9:2]), .data(insout[31:24]));
  ROM #(.addrWidth(8), .dataWidth(8), .Select("low")) RAM2 (.addr(pc_q[9:2]), .data(insout[23:16]));
  ROM #(.addrWidth(8), .dataWidth(8), .Select("low")) RAM1 (.addr(pc_q[9:2]), .data(insout[15:8]));
  ROM #(.addrWidth(8), .dataWidth(8), .Select("low")) RAM0 (.addr(pc_q[9:2]), .data(insout[7:0]));
  // Probe on insout

  // Other names for the same wires on the sheet: imm[15:0] = insout[15:0]; target_address[25:0] = insout[25:0]

  // Notes on the sheet:
  //   contents of RAM3 (hex, n*v repeats v):
  //   3c 3c 1 1 34 34 ac 8c 34 34 34 1 11 8 1 34 34 2 2 ac 8c
  //   contents of RAM2 (hex, n*v repeats v):
  //   8 9 9 49 b 1 2b 2c d e 10 b0 ae 0 ae 11 12 32 71 33 35
  //   contents of RAM1 (hex, n*v repeats v):
  //   0 0 50 50 7*0 68 0 c 78 0 0 98 a0
  //   contents of RAM0 (hex, n*v repeats v):
  //   ff 1 21 23 19 8 4 4 9 5 1 23 1 9 21 1 2 23 23 c c
endmodule

// 4bit-add
module _18020208_4bit_add (
  input  C0,
  input  A0,
  input  A1,
  input  A2,
  input  A3,
  input  B0,
  input  B1,
  input  B2,
  input  B3,
  output Sigma0,
  output Sigma1,
  output Sigma2,
  output Sigma3,
  output Gi_star,
  output Pi_star
);

  wire and_5_out, and_6_out, and_7_out, and_8_out, and_9_out, and_10_out, and_11_out, and_12_out, and_13_out,
       C1, C2, C3, G0, G1, G2, G3, P0, P1, P2, P3;

  and and_1 (G0, A0, B0);
  xor xor_1 (P0, A0, B0);
  and and_2 (G1, A1, B1);
  xor xor_2 (P1, A1, B1);
  and and_3 (G2, A2, B2);
  xor xor_3 (P2, A2, B2);
  and and_4 (G3, A3, B3);
  xor xor_4 (P3, A3, B3);
  and and_5 (and_5_out, C0, P0);
  and and_6 (and_6_out, C0, P0, P1);
  and and_7 (and_7_out, P1, G0);
  and and_8 (and_8_out, C0, P0, P1, P2);
  and and_9 (and_9_out, G0, P1, P2);
  and and_10 (and_10_out, P2, G1);
  and and_11 (and_11_out, G0, P1, P2, P3);
  and and_12 (and_12_out, P3, P2, G1);
  and and_13 (and_13_out, P3, G2);
  or or_1 (C1, and_5_out, G0);
  or or_2 (C2, and_6_out, and_7_out, G1);
  or or_3 (C3, and_8_out, and_9_out, and_10_out, G2);
  or or_4 (Gi_star, and_11_out, and_12_out, and_13_out, G3);
  and and_14 (Pi_star, P3, P2, P1, P0);
  xor xor_5 (Sigma0, C0, P0);
  xor xor_6 (Sigma1, C1, P1);
  xor xor_7 (Sigma2, C2, P2);
  xor xor_8 (Sigma3, C3, P3);
endmodule

// carry
module _18020208_Carry (
  input  C0,
  input  G0_star,
  input  P0_star,
  input  G1_star,
  input  P1_star,
  input  G2_star,
  input  P2_star,
  input  G3_star,
  input  P3_star,
  output C4,
  output C8,
  output C12,
  output C16
);

  wire and_1_out, and_2_out, and_3_out, and_4_out, and_5_out, and_6_out, and_7_out, and_8_out, and_9_out,
       and_10_out;

  and and_1 (and_1_out, C0, P0_star);
  and and_2 (and_2_out, P1_star, G0_star);
  and and_3 (and_3_out, P1_star, P0_star, C0);
  and and_4 (and_4_out, P2_star, G1_star);
  and and_5 (and_5_out, P2_star, P1_star, G0_star);
  and and_6 (and_6_out, P2_star, P1_star, P0_star, C0);
  and and_7 (and_7_out, P3_star, G2_star);
  and and_8 (and_8_out, P3_star, P2_star, G1_star);
  and and_9 (and_9_out, P3_star, P2_star, P1_star, G0_star);
  and and_10 (and_10_out, P3_star, P2_star, P1_star, P0_star, C0);
  or or_1 (C4, and_1_out, G0_star);
  or or_2 (C8, G1_star, and_2_out, and_3_out);
  or or_3 (C12, G2_star, and_4_out, and_5_out, and_6_out);
  or or_4 (C16, G3_star, and_7_out, and_8_out, and_9_out, and_10_out);
endmodule

// 16bit-add
module _18020208_16bit_add (
  input  C0,
  input  [15:0] A,
  input  [15:0] B,
  output out_4,
  output [15:0] res
);

  wire G0_star, G1_star, G2_star, G3_star, n18020208_carry_1_c4, n18020208_carry_1_c8, n18020208_carry_1_c12,
       P0_star, P1_star, P2_star, P3_star;

  _18020208_4bit_add u_18020208_4bit_add_1 (
    .C0(C0), .A0(A[0]), .A1(A[1]), .A2(A[2]), .A3(A[3]), .B0(B[0]), .B1(B[1]), .B2(B[2]), .B3(B[3]),
    .Sigma0(res[0]), .Sigma1(res[1]), .Sigma2(res[2]), .Sigma3(res[3]), .Gi_star(G0_star), .Pi_star(P0_star));
  _18020208_4bit_add u_18020208_4bit_add_2 (
    .C0(n18020208_carry_1_c4), .A0(A[4]), .A1(A[5]), .A2(A[6]), .A3(A[7]), .B0(B[4]), .B1(B[5]), .B2(B[6]),
    .B3(B[7]), .Sigma0(res[4]), .Sigma1(res[5]), .Sigma2(res[6]), .Sigma3(res[7]), .Gi_star(G1_star),
    .Pi_star(P1_star));
  _18020208_4bit_add u_18020208_4bit_add_3 (
    .C0(n18020208_carry_1_c8), .A0(A[8]), .A1(A[9]), .A2(A[10]), .A3(A[11]), .B0(B[8]), .B1(B[9]),
    .B2(B[10]), .B3(B[11]), .Sigma0(res[8]), .Sigma1(res[9]), .Sigma2(res[10]), .Sigma3(res[11]),
    .Gi_star(G2_star), .Pi_star(P2_star));
  _18020208_4bit_add u_18020208_4bit_add_4 (
    .C0(n18020208_carry_1_c12), .A0(A[12]), .A1(A[13]), .A2(A[14]), .A3(A[15]), .B0(B[12]), .B1(B[13]),
    .B2(B[14]), .B3(B[15]), .Sigma0(res[12]), .Sigma1(res[13]), .Sigma2(res[14]), .Sigma3(res[15]),
    .Gi_star(G3_star), .Pi_star(P3_star));
  _18020208_Carry u_18020208_carry_1 (
    .C0(C0), .G0_star(G0_star), .P0_star(P0_star), .G1_star(G1_star), .P1_star(P1_star), .G2_star(G2_star),
    .P2_star(P2_star), .G3_star(G3_star), .P3_star(P3_star), .C4(n18020208_carry_1_c4),
    .C8(n18020208_carry_1_c8), .C12(n18020208_carry_1_c12), .C16(out_4));

  // Other names for the same wires on the sheet: A_0_3[3:0] = A[3:0]; A_4_7[3:0] = A[7:4]; A_8_11[3:0] = A[11:8];
  //   A_12_15[3:0] = A[15:12]; B_0_3[3:0] = B[3:0]; B_4_7[3:0] = B[7:4]; B_8_11[3:0] = B[11:8];
  //   B_12_15[3:0] = B[15:12]
endmodule

// 32bit-add
module _18020208_32bit_add (
  input  [31:0] A,
  input  [31:0] B,
  output [31:0] res,
  output out_4
);

  wire n18020208_16bit_add_1_out_4;

  _18020208_16bit_add u_18020208_16bit_add_1 (
    .C0(1'b0), .A(A[15:0]), .B(B[15:0]), .out_4(n18020208_16bit_add_1_out_4), .res(res[15:0]));
  _18020208_16bit_add u_18020208_16bit_add_2 (
    .C0(n18020208_16bit_add_1_out_4), .A(A[31:16]), .B(B[31:16]), .out_4(out_4), .res(res[31:16]));

  // Other names for the same wires on the sheet: A_0_15[15:0] = A[15:0]; A_16_31[15:0] = A[31:16];
  //   B_0_15[15:0] = B[15:0]; B_16_31[15:0] = B[31:16]
endmodule

// 32bit-sub
module _18020208_32bit_sub (
  input  [31:0] A,
  input  [31:0] B,
  output [31:0] res,
  output out_4
);

  wire n18020208_16bit_add_1_out_4, n18020208_16bit_add_2_out_4;
  wire [15:0] B_0_15, B_16_31;

  assign {B_16_31, B_0_15} = ~B;  // NOT_Gate not_1, 32 bits wide
  _18020208_16bit_add u_18020208_16bit_add_1 (
    .C0(1'b1), .A(A[15:0]), .B(B_0_15), .out_4(n18020208_16bit_add_1_out_4), .res(res[15:0]));
  _18020208_16bit_add u_18020208_16bit_add_2 (
    .C0(n18020208_16bit_add_1_out_4), .A(A[31:16]), .B(B_16_31), .out_4(n18020208_16bit_add_2_out_4),
    .res(res[31:16]));
  not not_2 (out_4, n18020208_16bit_add_2_out_4);

  // Other names for the same wires on the sheet: A_0_15[15:0] = A[15:0]; A_16_31[15:0] = A[31:16]
endmodule

// ALU
module _18020208_ALU (
  input  [31:0] A,
  input  [1:0] ALUctr,
  input  [31:0] B,
  output [31:0] result
);

  wire [31:0] n18020208_32bit_add_1_res, n18020208_32bit_sub_1_res, ori_out;

  _18020208_32bit_add u_18020208_32bit_add_1 (.A(A), .B(B), .res(n18020208_32bit_add_1_res));  // open: out_4
  _18020208_32bit_sub u_18020208_32bit_sub_1 (.A(A), .B(B), .res(n18020208_32bit_sub_1_res));  // open: out_4
  assign ori_out = A | B;  // OR_Gate ori, 32 bits wide
  Multiplexer #(.select(2), .width(32), .disabled("Z"), .enable("false")) multiplexer_1 (
    .in0(n18020208_32bit_add_1_res), .in1(n18020208_32bit_sub_1_res), .in2(ori_out), .out(result),
    .sel(ALUctr));  // open: in3
endmodule

// EXT
module _18020208_EXT (
  input  [15:0] A,
  input  [1:0] ExtOp,
  output [31:0] B
);

  wire [31:0] bit_extender_1_out, bit_extender_2_out;

  assign bit_extender_1_out = {{16{1'b0}}, A};  // Bit_Extender bit_extender_1
  assign bit_extender_2_out = {{16{A[15]}}, A};  // Bit_Extender bit_extender_2
  Multiplexer #(.select(2), .width(32), .disabled("Z"), .enable("false")) multiplexer_1 (
    .in0(bit_extender_1_out), .in1(bit_extender_2_out), .in2({A, {16{1'b0}}}), .in3({A, {16{1'b0}}}),
    .out(B), .sel(ExtOp));

  // Notes on the sheet:
  //   00：高位零扩展01：符号扩展10：低位零扩展
endmodule

// DM
module _18020208_DM (
  input  in_1,
  input  in_2,
  input  in_3,
  input  [31:0] addr,
  input  [31:0] data_in,
  output [31:0] out_6
);

  RAM #(.addrWidth(8), .dataWidth(8), .bus("separate"), .Select("low")) RAM3 (
    .addr(addr[9:2]), .din(data_in[7:0]), .data(out_6[7:0]), .str(in_3), .clk(in_2), .clr(in_1));  // open: sel, ld
  RAM #(.addrWidth(8), .dataWidth(8), .bus("separate"), .Select("low")) RAM2 (
    .addr(addr[9:2]), .din(data_in[15:8]), .data(out_6[15:8]), .str(in_3), .clk(in_2), .clr(in_1));  // open: sel, ld
  RAM #(.addrWidth(8), .dataWidth(8), .bus("separate"), .Select("low")) RAM1 (
    .addr(addr[9:2]), .din(data_in[23:16]), .data(out_6[23:16]), .str(in_3), .clk(in_2), .clr(in_1));  // open: sel, ld
  RAM #(.addrWidth(8), .dataWidth(8), .bus("separate"), .Select("low")) RAM0 (
    .addr(addr[9:2]), .din(data_in[31:24]), .data(out_6[31:24]), .str(in_3), .clk(in_2), .clr(in_1));  // open: sel, ld
  // Probe on out_6

  // Other names for the same wires on the sheet: clk = in_2; MemWr = in_3; reset = in_1
endmodule

module _18020208_CONTROL (
  input  [5:0] opcode,
  input  [5:0] \function ,
  output RegDst,
  output ALUSrc,
  output MemtoReg,
  output RegWrite,
  output MemWrite,
  output npc_sel,
  output [1:0] ExtOp,
  output [1:0] ALUCtr,
  output j
);

  wire addu_out, subu_out;

  and ori (ALUCtr[1], opcode[0], ~opcode[1], opcode[2], opcode[2], ~opcode[4], ~opcode[5]);  // AND_Gate
  and addu (addu_out, ~opcode[0], ~opcode[1], ~opcode[2], ~opcode[3], ~opcode[4], ~opcode[5], \function [0], ~\function [1], ~\function [2], ~\function [3], ~\function [4], \function [5]);  // AND_Gate
  and subu (subu_out, ~opcode[0], ~opcode[1], ~opcode[2], ~opcode[3], ~opcode[4], ~opcode[5], \function [0], \function [1], ~\function [2], ~\function [3], ~\function [4], \function [5]);  // AND_Gate
  and lw (MemtoReg, opcode[0], opcode[1], ~opcode[2], ~opcode[3], ~opcode[4], opcode[5]);  // AND_Gate
  and sw (MemWrite, opcode[0], opcode[1], ~opcode[2], opcode[3], ~opcode[4], opcode[5]);  // AND_Gate
  and beq (npc_sel, ~opcode[0], ~opcode[1], opcode[2], ~opcode[3], ~opcode[4], ~opcode[5]);  // AND_Gate
  and lui (ExtOp[1], opcode[0], opcode[1], opcode[2], opcode[3], ~opcode[4], ~opcode[5]);  // AND_Gate
  and u_j (j, ~opcode[0], opcode[1], ~opcode[2], ~opcode[3], ~opcode[4], ~opcode[5]);  // AND_Gate
  or u_RegDst (RegDst, addu_out, subu_out);
  or u_ALUSrc (ALUSrc, ALUCtr[1], MemtoReg, MemWrite, ExtOp[1]);
  or u_RegWrite (RegWrite, addu_out, subu_out, ExtOp[1], ALUCtr[1], MemtoReg);
  or or_1 (ExtOp[0], MemtoReg, MemWrite);
  or or_2 (ALUCtr[0], subu_out, npc_sel);
endmodule
